# Fritzing sketch sketch (saved by Fritzing 0.9.3b)
breadboards: 1

parts:
  Mega_2560 = Arduino Mega 2560 (Rev3)
  Receptor_Bluetooth = Bluetooth HC-05 Macho
  U2 = LCD-16X2 [package=lcd-16x2_noholes]
  R1 = Resistor [tolerance=±5% resistance=1k package=THT]
  R2 = Resistor [tolerance=±5% resistance=2.2k package=THT]

nets:
  N1: Mega_2560.D11_PWM, Receptor_Bluetooth.RXD
  N2: Mega_2560.D10_PWM, Receptor_Bluetooth.TXD
  N3: Mega_2560.D2_PWM, U2.DB7
  N4: Mega_2560.D3_PWM, U2.DB6
  N5: Mega_2560.D4_PWM, U2.DB5
  N6: Mega_2560.D5_PWM, U2.DB4
  N7: Mega_2560.D6_PWM, U2.E
  N8: Mega_2560.D7_PWM, U2.RS
  VCC: Receptor_Bluetooth.VCC, U2.VDD, U2.K
  GND: Receptor_Bluetooth.GND, U2.VSS, U2.R_W, R1.Pin_1, R2.Pin_0
  N9: U2.VO, R2.Pin_1
  N10: U2.A, R1.Pin_0
